// Logisim project Lab2.circ as structural Verilog: 2 circuits, main circuit Lab 2 Part 1
module Lab_2_Part_1 (
  input  a1,
  input  a0,
  input  b1,
  input  b0,
  input  [1:0] b1_b0,
  input  [1:0] a1_a0,
  input  a1_2,
  input  a0_2,
  input  b1_2,
  input  b0_2,
  output out,
  output out_12,
  output out_13
);

  wire and_1_out, and_2_out, and_3_out, and_4_out, and_5_out, not_1_out, not_2_out, not_3_out, not_4_out,
       not_5_out;

  not not_1 (not_1_out, a1);
  and and_1 (and_1_out, not_1_out, not_2_out);
  not not_2 (not_2_out, a0);
  not not_3 (not_3_out, a1);
  and and_2 (and_2_out, not_3_out, b0);
  not not_4 (not_4_out, a1);
  and and_3 (and_3_out, not_4_out, b1);
  not not_5 (not_5_out, a0);
  and and_4 (and_4_out, not_5_out, b1);
  and and_5 (and_5_out, b1, b0);
  or or_1 (out, and_1_out, and_2_out, and_3_out, and_4_out, and_5_out);
  Multiplexer #(.select(3), .enable("false")) multiplexer_1 (
    .in0(1'b1), .in1(1'b1), .in2(b0_2), .in3(1'b1), .in4(1'b0), .in5(1'b1), .in6(1'b0), .in7(b0_2),
    .out(out_13), .sel({a1_2, a0_2, b1_2}));
  ROM #(.addrWidth(4), .dataWidth(1)) rom_1 (.addr({a1_a0, b1_b0}), .data(out_12));  // open: sel

  // Notes on the sheet:
  //   contents of rom_1 (hex, n*v repeats v):
  //   4*1 0 1 1 1 0 0 1 1 0 0 0 1
endmodule

module Lab_2_Part_2 (
  input  X,
  input  Y,
  input  Z,
  input  [2:0] in_4,
  input  X_2,
  input  Y_2,
  input  Z_2,
  output out,
  output out_9,
  output out_10
);

  wire and_1_out, and_2_out, and_3_out, not_1_out, not_2_out, not_3_out, not_4_out, not_5_out, not_6_out;

  not not_1 (not_1_out, X);
  not not_2 (not_2_out, Y);
  not not_3 (not_3_out, X);
  not not_4 (not_4_out, Z);
  not not_5 (not_5_out, Y);
  not not_6 (not_6_out, Z);
  and and_1 (and_1_out, not_1_out, not_2_out);
  and and_2 (and_2_out, not_3_out, not_4_out);
  and and_3 (and_3_out, not_5_out, not_6_out);
  Multiplexer #(.select(3), .enable("false")) multiplexer_1 (
    .in0(1'b1), .in1(1'b1), .in2(1'b1), .in3(1'b0), .in4(1'b1), .in5(1'b0), .in6(1'b0), .in7(1'b0),
    .out(out_9), .sel({X_2, Y_2, Z_2}));
  or or_1 (out, and_1_out, and_2_out, and_3_out);
  ROM #(.addrWidth(3), .dataWidth(1)) rom_1 (.addr(in_4), .data(out_10));  // open: sel

  // Notes on the sheet:
  //   contents of rom_1 (hex, n*v repeats v):
  //   1 1 1 0 1
endmodule
