// Logisim project Lab3.circ as structural Verilog: 1 circuit, main circuit main
module main (
);

  wire clock_1_out;
  wire [4:0] register_1_q;
  wire [6:0] rom_1_data;

  ROM #(.addrWidth(5), .dataWidth(7)) rom_1 (.addr(register_1_q), .data(rom_1_data));  // open: sel
  Clock clock_1 (.out(clock_1_out));
  Register #(.width(5)) register_1 (.D(rom_1_data[4:0]), .Q(register_1_q), .clk(clock_1_out));  // open: en, clr

  // Notes on the sheet:
  //   contents of rom_1 (hex, n*v repeats v):
  //   0 10 20 8 10 20 30 9 20 30 40 a 30 40 8 b 40 8 9 c
endmodule
