// Logisim project Register State Machine Input.circ as structural Verilog: 2 circuits, main circuit main
module main (
);

  wire clock_1_out;
  wire [1:0] register_1_q, rom_1_data;

  ROM #(.addrWidth(2), .dataWidth(2)) rom_1 (.addr(register_1_q), .data(rom_1_data));  // open: sel
  Clock clock_1 (.out(clock_1_out));
  Register #(.width(2)) register_1 (.D(rom_1_data), .Q(register_1_q), .clk(clock_1_out));  // open: en, clr

  // Notes on the sheet:
  //   Transition
  //   Current State
  //   contents of rom_1 (hex, n*v repeats v):
  //   1 2 3
  //   Next
  //   Cause State Transition
endmodule

module take_inputs (
  input  in_1,
  output out_2
);

  wire clock_1_out;
  wire [1:0] register_1_q, rom_1_data;

  ROM #(.addrWidth(3), .dataWidth(3)) rom_1 (.addr({register_1_q, in_1}), .data({out_2, rom_1_data}));  // open: sel
  Register #(.width(2)) register_1 (.D(rom_1_data), .Q(register_1_q), .clk(clock_1_out));  // open: en, clr
  Clock clock_1 (.out(clock_1_out));

  // Notes on the sheet:
  //   contents of rom_1 (hex, n*v repeats v):
  //   1 0 6 0 2 1 3 3
endmodule
