// Logisim project StateMachine(1.29).circ as structural Verilog: 1 circuit, main circuit main
module main (
  input  in_1,
  output out_2
);

  wire clock_1_out;
  wire [1:0] register_1_q;
  wire [2:1] rom_1_data;

  ROM #(.addrWidth(3), .dataWidth(3)) rom_1 (.addr({register_1_q, in_1}), .data({rom_1_data, out_2}));  // open: sel
  Clock clock_1 (.out(clock_1_out));
  Register #(.width(2)) register_1 (.D(rom_1_data), .Q(register_1_q), .clk(clock_1_out));  // open: en, clr

  // Notes on the sheet:
  //   contents of rom_1 (hex, n*v repeats v):
  //   0 4 6 4 3 6 7 6
endmodule
